# Fritzing sketch Combined (saved by Fritzing 0.9.3b)
breadboards: 2

parts:
  M1 = Stepper Motor - Bipolar
  M2 = Stepper Motor - Bipolar
  Pololu_A1 = Pololu A4988 [package=SO16]
  Pololu_A2 = Pololu A4988 [package=SO16]
  C1 = Electrolytic Capacitor [capacitance=10μF package="0605 [SMD, electrolytic]"]
  Part1 = Arduino Mega 2560 (Rev3)
  Part2 = NRF24L01+ Breakout Board
  Part3 = NRF24L01+ Breakout Board
  Part4 = Thumb Joystick
  Part5 = Arduino Uno (Rev3) - ICSP
  R1 = Resistor [tolerance=±5% resistance=220 package="0402 [SMD]"]
  LED1 = smd LED [color="Red (633nm)" package="1206 [SMD]"]
  LED2 = smd LED [color="Red (633nm)" package="1206 [SMD]"]
  LED3 = smd LED [color="Red (633nm)" package="1206 [SMD]"]
  LED4 = smd LED [color="Red (633nm)" package="1206 [SMD]"]
  LED5 = smd LED [color="Red (633nm)" package="1206 [SMD]"]
  R2 = Resistor [tolerance=±5% resistance=220 package="0805 [SMD]"]
  R3 = Resistor [tolerance=±5% resistance=220 package="0805 [SMD]"]
  R4 = Resistor [tolerance=±5% resistance=220 package="0805 [SMD]"]
  R5 = Resistor [tolerance=±5% resistance=220 package="0805 [SMD]"]
  R6 = Resistor [tolerance=±5% resistance=220 package="0805 [SMD]"]
  S1 = SWITCH-MOMENTARY-2 [package=tactile-switch-1101ne]
  R7 = Resistor [tolerance=±5% resistance=220 package="0805 [SMD]"]
  J1 = Piezo Speaker
  LED6 = smd LED [color="Red (633nm)" package="1206 [SMD]"]
  LED7 = smd LED [color="Red (633nm)" package="1206 [SMD]"]
  LED8 = smd LED [color="Red (633nm)" package="1206 [SMD]"]
  R8 = Resistor [tolerance=±5% resistance=220 package="0805 [SMD]"]
  J2 = Piezo Speaker
  R9 = Resistor [tolerance=±5% resistance=220 package=THT]
  R10 = Resistor [tolerance=±5% resistance=220 package=THT]
  R11 = Resistor [tolerance=±5% resistance=220 package=THT]

nets:
  N1: M1.A, Pololu_A2.2B
  N2: M1.C, Pololu_A2.2A
  N3: M1.B, Pololu_A2.1A
  N4: M1.D, Pololu_A2.1B
  N5: M2.A, Pololu_A1.2B
  N6: M2.C, Pololu_A1.2A
  N7: M2.B, Pololu_A1.1A
  N8: M2.D, Pololu_A1.1B
  N9: Pololu_A1.RESET, Pololu_A1.SLEEP
  N10: Pololu_A1.STEP, Part1.D4_PWM
  N11: Pololu_A1.DIR, Part1.D3_PWM
  GND: Pololu_A1.GND, Pololu_A1.VMOT, Pololu_A2.GND, Pololu_A2.VMOT, C1.-, LED1.cathode, LED2.cathode, LED3.cathode, LED4.cathode, LED5.cathode, R7.Pin_0, R9.Pin_1
  VDD: Pololu_A1.VDD, Pololu_A2.VDD, S1.1
  N12: Pololu_A2.RESET, Pololu_A2.SLEEP
  N13: Pololu_A2.STEP, Part1.D6_PWM
  N14: Pololu_A2.DIR, Part1.D5_PWM
  N15: Part1.D21/SCL, J1.pin2
  N16: Part1.D12_PWM, S1.2, R9.Pin_0
  N17: Part1.D9_PWM, R2.Pin_1, R3.Pin_1, R4.Pin_1, R5.Pin_1, R6.Pin_1
  N18: Part1.D8_PWM, Part2.CS
  3V3: Part1.3V3, Part2.VCC
  GND_2: Part1.GND, Part2.GND
  N19: Part1.D7_PWM, Part2.CE
  N20: Part1.D50, Part2.MISO
  N21: Part1.D51, Part2.MOSI
  N22: Part1.D52, Part2.SCK
  GND_3: Part3.GND, Part4.GND, Part5.GND, R8.Pin_0
  VCC: Part3.VCC, Part5.3V3
  N23: Part3.CE, Part5.D7
  N24: Part3.CS, Part5.D8
  N25: Part3.SCK, Part5.D13/SCK
  N26: Part3.MOSI, Part5.D11_PWM/MOSI
  N27: Part3.MISO, Part5.D12/MISO
  N28: Part4.SEL, Part5.D2, R1.Pin_1
  N29: Part4.HORZ, Part5.A0
  N30: Part4.VERT, Part5.A1
  VCC_2: Part4.VCC, Part5.5V, R1.Pin_0
  N31: Part5.D3_PWM, LED8.cathode
  N32: Part5.D4, J2.pin2
  N33: Part5.D5_PWM, LED6.cathode
  N34: Part5.D6_PWM, LED7.cathode
  N35: LED1.anode, R2.Pin_0
  N36: LED2.anode, R3.Pin_0
  N37: LED3.anode, R4.Pin_0
  N38: LED4.anode, R5.Pin_0
  N39: LED5.anode, R6.Pin_0
  N40: R7.Pin_1, J1.pin1
  N41: LED6.anode, R10.Pin_0, R11.Pin_1
  N42: LED7.anode, R11.Pin_0
  N43: LED8.anode, R8.Pin_1, J2.pin1, R10.Pin_1
